// Logisim project ALU.circ as structural Verilog: 10 circuits, main circuit ALU
module ALU (
  input  OP,
  input  [7:0] A,
  input  [7:0] B,
  output [7:0] R,
  output C,
  output V
);

  wire [7:0] xor_1_out;

  assign xor_1_out = {8{OP}} ^ B;  // XOR_Gate xor_1, 8 bits wide
  Add8bits add8bits_1 (.in_1(OP), .in_2(A), .in_3(xor_1_out), .out_4(R), .C_out(C));
  overflow overflow_1 (.in_1(A[7]), .in_2(xor_1_out[7]), .in_3(R[7]), .V(V));
endmodule

module Add1bit (
  input  A,
  input  B,
  input  C_in,
  output D,
  output C_out
);

  wire AND_2_out, AND_3_out, AND_out, XOR_out;

  xor XOR (XOR_out, A, B);
  and AND (AND_out, A, B);
  and AND_2 (AND_2_out, A, C_in);
  and AND_3 (AND_3_out, B, C_in);
  xor XOR_2 (D, XOR_out, C_in);
  or OR (C_out, AND_out, AND_2_out, AND_3_out);
endmodule

module Add4bits (
  input  C_in,
  input  [3:0] A,
  input  [3:0] B,
  output [3:0] S,
  output C_out
);

  wire add1bit_1_c_out, add1bit_2_c_out, add1bit_3_c_out;

  Add1bit add1bit_1 (.A(A[0]), .D(S[0]), .B(B[0]), .C_in(C_in), .C_out(add1bit_1_c_out));
  Add1bit add1bit_2 (.A(A[1]), .D(S[1]), .B(B[1]), .C_in(add1bit_1_c_out), .C_out(add1bit_2_c_out));
  Add1bit add1bit_3 (.A(A[2]), .D(S[2]), .B(B[2]), .C_in(add1bit_2_c_out), .C_out(add1bit_3_c_out));
  Add1bit add1bit_4 (.A(A[3]), .D(S[3]), .B(B[3]), .C_in(add1bit_3_c_out), .C_out(C_out));
endmodule

module Add8bits (
  input  in_1,
  input  [7:0] in_2,
  input  [7:0] in_3,
  output [7:0] out_4,
  output C_out
);

  wire add4bits_1_c_out;

  Add4bits add4bits_1 (.C_in(in_1), .A(in_2[3:0]), .B(in_3[3:0]), .S(out_4[3:0]), .C_out(add4bits_1_c_out));
  Add4bits add4bits_2 (.C_in(add4bits_1_c_out), .A(in_2[7:4]), .B(in_3[7:4]), .S(out_4[7:4]), .C_out(C_out));
endmodule

module Sous8bits (
  input  [7:0] A,
  input  [7:0] B,
  output [7:0] out_3
);

  wire add8bits_1_p3;
  wire [7:0] not_1_out;

  assign not_1_out = ~B;  // NOT_Gate not_1, 8 bits wide
  // Add8bits add8bits_1: pin names not known; wires that end beside it: A, not_1_out, add8bits_1_p3
  // Add8bits add8bits_2: pin names not known; wires that end beside it: add8bits_1_p3, 8'h1, out_3
endmodule

module overflow (
  input  in_1,
  input  in_2,
  input  in_3,
  output V
);

  wire and_1_out, and_2_out, not_1_out, not_2_out, not_3_out;

  not not_1 (not_1_out, in_3);
  not not_2 (not_2_out, in_1);
  not not_3 (not_3_out, in_2);
  and and_1 (and_1_out, in_1, in_2, not_1_out);
  and and_2 (and_2_out, not_2_out, not_3_out, in_3);
  or or_1 (V, and_1_out, and_2_out);
endmodule

module ALUComplexe (
  input  [2:0] OP,
  input  [7:0] A,
  input  [7:0] B,
  output Z,
  output N,
  output [7:0] R,
  output C,
  output V
);

  wire A_Shift_Right_c, alu_1_c, Shift_Left_c, Shift_Right_c;
  wire [7:0] A_Shift_Right_out_3, alu_1_r, ETbb_out, NON_out, OUbb_out, Shift_Left_out_2, Shift_Right_out_3;

  ALU alu_1 (.OP(OP[0]), .A(A), .B(B), .R(alu_1_r), .C(alu_1_c), .V(V));
  ShiftLeft Shift_Left (.A(A), .out_2(Shift_Left_out_2), .C(Shift_Left_c));
  ShiftRight Shift_Right (.A(A), .C(Shift_Right_c), .out_3(Shift_Right_out_3));
  ArithmetiqueShiftRight A_Shift_Right (.A(A), .C(A_Shift_Right_c), .out_3(A_Shift_Right_out_3));
  assign ETbb_out = A & B;  // AND_Gate ETbb, 8 bits wide
  assign OUbb_out = A | B;  // OR_Gate OUbb, 8 bits wide
  assign NON_out = ~A;  // NOT_Gate NON, 8 bits wide
  Multiplexer #(.select(3)) multiplexer_1 (
    .in0(alu_1_c), .in1(alu_1_c), .in2(Shift_Left_c), .in3(Shift_Right_c), .in4(A_Shift_Right_c), .in5(1'b0),
    .in6(1'b0), .in7(1'b0), .out(C), .sel(OP));  // open: en
  Multiplexer #(.select(3), .width(8)) multiplexer_2 (
    .in0(alu_1_r), .in1(alu_1_r), .in2(Shift_Left_out_2), .in3(Shift_Right_out_3), .in4(A_Shift_Right_out_3),
    .in5(ETbb_out), .in6(OUbb_out), .in7(NON_out), .out({N, R[6:0]}), .sel(OP));  // open: en
  and and_1 (Z, ~R[0], ~R[1], ~R[2], ~R[3], ~R[5], ~R[5], ~R[6], ~N);  // AND_Gate

  assign R[7] = N;
endmodule

module ShiftLeft (
  input  [7:0] A,
  output [7:0] out_2,
  output C
);


  assign C = A[7];
  assign out_2 = {A[6:0], 1'b0};
endmodule

module ShiftRight (
  input  [7:0] A,
  output C,
  output [7:0] out_3
);


  assign C = A[0];
  assign out_3 = {1'b0, A[7:1]};
endmodule

module ArithmetiqueShiftRight (
  input  [7:0] A,
  output C,
  output [7:0] out_3
);


  assign C = A[0];
  assign out_3 = {{2{A[7]}}, A[6:1]};
endmodule
