// Logisim project memoire.circ as structural Verilog: 2 circuits, main circuit memoire
module memoire (
  input  [2:0] A,
  input  [2:0] B,
  input  [2:0] AddressWrite,
  input  [7:0] WriteValue,
  input  AllowWrite,
  input  Reset,
  input  clk,
  output [7:0] OutA,
  output [7:0] OutB
);

  wire demultiplexer_1_out0, demultiplexer_1_out1, demultiplexer_1_out2, demultiplexer_1_out3,
       demultiplexer_1_out4, demultiplexer_1_out5, demultiplexer_1_out6, demultiplexer_1_out7;
  wire [7:0] Reg0_q, Reg1_q, Reg2_q, Reg3_q, Reg4_q, Reg5_q, Reg6_q, Reg7_q;

  Demultiplexer #(.select(3)) demultiplexer_1 (
    .out0(demultiplexer_1_out0), .out1(demultiplexer_1_out1), .out2(demultiplexer_1_out2),
    .out3(demultiplexer_1_out3), .out4(demultiplexer_1_out4), .out5(demultiplexer_1_out5),
    .out6(demultiplexer_1_out6), .out7(demultiplexer_1_out7), .in(AllowWrite), .sel(AddressWrite));  // open: en
  Register Reg0 (.D(WriteValue), .en(demultiplexer_1_out0), .clk(clk), .Q(Reg0_q), .clr(Reset));
  Register Reg1 (.D(WriteValue), .en(demultiplexer_1_out1), .clk(clk), .Q(Reg1_q), .clr(Reset));
  Register Reg2 (.D(WriteValue), .en(demultiplexer_1_out2), .clk(clk), .Q(Reg2_q), .clr(Reset));
  Register Reg3 (.D(WriteValue), .en(demultiplexer_1_out3), .clk(clk), .Q(Reg3_q), .clr(Reset));
  Register Reg4 (.D(WriteValue), .en(demultiplexer_1_out4), .clk(clk), .Q(Reg4_q), .clr(Reset));
  Register Reg5 (.D(WriteValue), .en(demultiplexer_1_out5), .clk(clk), .Q(Reg5_q), .clr(Reset));
  Register Reg6 (.D(WriteValue), .en(demultiplexer_1_out6), .clk(clk), .Q(Reg6_q), .clr(Reset));
  Register Reg7 (.D(WriteValue), .en(demultiplexer_1_out7), .clk(clk), .Q(Reg7_q), .clr(Reset));
  Multiplexer #(.select(3), .width(8)) multiplexer_1 (
    .in0(Reg0_q), .in1(Reg1_q), .in2(Reg2_q), .in3(Reg3_q), .in4(Reg4_q), .in5(Reg5_q), .in6(Reg6_q),
    .in7(Reg7_q), .out(OutA), .sel(A));  // open: en
  Multiplexer #(.select(3), .width(8)) multiplexer_2 (
    .in0(Reg0_q), .in1(Reg1_q), .in2(Reg2_q), .in3(Reg3_q), .in4(Reg4_q), .in5(Reg5_q), .in6(Reg6_q),
    .in7(Reg7_q), .out(OutB), .sel(B));  // open: en

  // Other names for the same wires on the sheet: AddressA[2:0] = A; AddressB[2:0] = B; Rst = Reset;
  //   WV[7:0] = WriteValue
endmodule

module rom (
  input  [3:0] Address,
  output [15:0] value
);

  Multiplexer #(.select(4), .width(16)) multiplexer_1 (
    .in0(16'h8240), .in1(16'h84bf), .in2(16'hd200), .in3(16'hd401), .in4({16{1'b1}}), .in5(16'hca03),
    .in6(16'hda00), .in7(16'hda01), .in8({16{1'b1}}), .in9({16{1'b1}}), .in10({16{1'b1}}), .in11({16{1'b1}}),
    .in12({16{1'b1}}), .in13({16{1'b1}}), .in14({16{1'b1}}), .in15({16{1'b1}}), .out(value), .sel(Address));  // open: en
endmodule
