// Logisim project adc.circ as structural Verilog: 1 circuit, main circuit tlc548
module tlc548 (
  input  clk,
  input  data_in,
  output cs,
  output io_clock,
  output [7:0] value
);
endmodule
