// Logisim project audio_out.circ as structural Verilog: 1 circuit, main circuit cs4344_mono
module cs4344_mono (
  input  clk,
  input  rst,
  input  [15:0] audio_in,
  output done,
  output SDOUT,
  output SCLK,
  output MCLK,
  output LRCK
);
endmodule
