// Logisim project compiled.circ as structural Verilog: 1 circuit, main circuit rom
module rom (
  input  [6:0] addr,
  output [15:0] data_out
);

  wire [15:0] mux0, mux1, mux2, mux3, undriven, undriven_2, undriven_3, undriven_4, undriven_5, undriven_6,
       undriven_7, undriven_8, undriven_9, undriven_10, undriven_11, undriven_12, undriven_13, undriven_14,
       undriven_15, undriven_16, undriven_17, undriven_18, undriven_19, undriven_20, undriven_21,
       undriven_22, undriven_23, undriven_24, undriven_25, undriven_26, undriven_27, undriven_28,
       undriven_29, undriven_30, undriven_31, undriven_32, undriven_33, undriven_34, undriven_35,
       undriven_36, undriven_37, undriven_38, undriven_39, undriven_40, undriven_41, undriven_42,
       undriven_43, undriven_44, undriven_45, undriven_46, undriven_47, undriven_48, undriven_49,
       undriven_50, undriven_51, undriven_52, undriven_53, undriven_54, undriven_55, undriven_56,
       undriven_57, undriven_58, undriven_59, undriven_60, undriven_61, undriven_62, undriven_63,
       undriven_64, undriven_65, undriven_66, undriven_67, undriven_68, undriven_69, undriven_70,
       undriven_71, undriven_72, undriven_73, undriven_74, undriven_75, undriven_76, undriven_77,
       undriven_78, undriven_79, undriven_80, undriven_81, undriven_82, undriven_83, undriven_84,
       undriven_85, undriven_86, undriven_87, undriven_88, undriven_89, undriven_90, undriven_91,
       undriven_92, undriven_93, undriven_94, undriven_95, undriven_96, undriven_97, undriven_98,
       undriven_99, undriven_100, undriven_101, undriven_102, undriven_103, undriven_104, undriven_105,
       undriven_106, undriven_107, undriven_108, undriven_109, undriven_110, undriven_111, undriven_112,
       undriven_113, undriven_114, undriven_115, undriven_116, undriven_117, undriven_118, undriven_119,
       undriven_120, undriven_121, undriven_122;

  Multiplexer #(.select(5), .width(16)) multiplexer_1 (
    .in0(16'hc000), .in1(16'hc201), .in2(16'h2000), .in3(16'hd006), .in4(16'hd207), .in5(16'hbffb),
    .in6(undriven), .in7(undriven_30), .in8(undriven_2), .in9(undriven_31), .in10(undriven_3),
    .in11(undriven_32), .in12(undriven_4), .in13(undriven_33), .in14(undriven_5), .in15(undriven_34),
    .in16(undriven_6), .in17(undriven_35), .in18(undriven_7), .in19(undriven_36), .in20(undriven_8),
    .in21(undriven_37), .in22(undriven_9), .in23(undriven_38), .in24(undriven_10), .in25(undriven_39),
    .in26(undriven_11), .in27(undriven_40), .in28(undriven_12), .in29(undriven_41), .in30(undriven_13),
    .in31(undriven_42), .out(mux0), .sel(addr[4:0]));  // open: en
  Multiplexer #(.select(5), .width(16)) multiplexer_2 (
    .in0(undriven_14), .in1(undriven_43), .in2(undriven_15), .in3(undriven_44), .in4(undriven_16),
    .in5(undriven_45), .in6(undriven_17), .in7(undriven_46), .in8(undriven_18), .in9(undriven_47),
    .in10(undriven_19), .in11(undriven_48), .in12(undriven_20), .in13(undriven_49), .in14(undriven_21),
    .in15(undriven_50), .in16(undriven_22), .in17(undriven_51), .in18(undriven_23), .in19(undriven_52),
    .in20(undriven_24), .in21(undriven_53), .in22(undriven_25), .in23(undriven_54), .in24(undriven_26),
    .in25(undriven_55), .in26(undriven_27), .in27(undriven_56), .in28(undriven_28), .in29(undriven_57),
    .in30(undriven_29), .in31(undriven_58), .out(mux1), .sel(addr[4:0]));  // open: en
  Multiplexer #(.select(5), .width(16)) multiplexer_3 (
    .in0(undriven_59), .in1(undriven_91), .in2(undriven_60), .in3(undriven_92), .in4(undriven_61),
    .in5(undriven_93), .in6(undriven_62), .in7(undriven_94), .in8(undriven_63), .in9(undriven_95),
    .in10(undriven_64), .in11(undriven_96), .in12(undriven_65), .in13(undriven_97), .in14(undriven_66),
    .in15(undriven_98), .in16(undriven_67), .in17(undriven_99), .in18(undriven_68), .in19(undriven_100),
    .in20(undriven_69), .in21(undriven_101), .in22(undriven_70), .in23(undriven_102), .in24(undriven_71),
    .in25(undriven_103), .in26(undriven_72), .in27(undriven_104), .in28(undriven_73), .in29(undriven_105),
    .in30(undriven_74), .in31(undriven_106), .out(mux2), .sel(addr[4:0]));  // open: en
  Multiplexer #(.select(5), .width(16)) multiplexer_4 (
    .in0(undriven_75), .in1(undriven_107), .in2(undriven_76), .in3(undriven_108), .in4(undriven_77),
    .in5(undriven_109), .in6(undriven_78), .in7(undriven_110), .in8(undriven_79), .in9(undriven_111),
    .in10(undriven_80), .in11(undriven_112), .in12(undriven_81), .in13(undriven_113), .in14(undriven_82),
    .in15(undriven_114), .in16(undriven_83), .in17(undriven_115), .in18(undriven_84), .in19(undriven_116),
    .in20(undriven_85), .in21(undriven_117), .in22(undriven_86), .in23(undriven_118), .in24(undriven_87),
    .in25(undriven_119), .in26(undriven_88), .in27(undriven_120), .in28(undriven_89), .in29(undriven_121),
    .in30(undriven_90), .in31(undriven_122), .out(mux3), .sel(addr[4:0]));  // open: en
  Multiplexer #(.select(2), .width(16)) multiplexer_5 (
    .in0(mux0), .in1(mux1), .in2(mux2), .in3(mux3), .out(data_out), .sel(addr[6:5]));  // open: en
  // Probe on data_out

  // Other names for the same wires on the sheet: sel[1:0] = addr[6:5]
endmodule
