// Logisim project seven_segments.circ as structural Verilog: 3 circuits, main circuit seven_segments_decode
module seven_segments_decode (
  input  [3:0] Input,
  output [6:0] decoded
);

  Multiplexer #(.select(4), .width(7), .enable("false")) multiplexer_1 (
    .in0(7'b0111111), .in1(7'b0000110), .in2(7'b1011011), .in3(7'b1001111), .in4(7'b1100110),
    .in5(7'b1101101), .in6(7'b1111101), .in7(7'b0000111), .in8({7{1'b1}}), .in9(7'b1101111),
    .in10(7'b1110111), .in11(7'b1111100), .in12(7'b0111001), .in13(7'b1011110), .in14(7'b1111001),
    .in15(7'b1110001), .out(decoded), .sel(Input));
endmodule

module seven_segment_scan (
  input  [6:0] display0,
  input  enable_display_0,
  input  [6:0] display1,
  input  enable_display_1,
  input  [6:0] display2,
  input  enable_display_2,
  input  [6:0] display3,
  input  enable_display_3,
  input  Reset,
  input  Enable,
  input  Clk,
  output [6:0] cathodes,
  output anode0,
  output anode1,
  output anode2,
  output anode3
);

  wire comparator_1_eq, decoder_1_out0, decoder_1_out1, decoder_1_out2, decoder_1_out3;
  wire [1:0] counter_2_q;
  wire [16:0] counter_1_q;

  Counter #(.width(17), .max('h1ffff)) counter_1 (
    .clr(Reset), .load(comparator_1_eq), .up(1'b1), .count(Enable), .clk(Clk), .D({17{1'b0}}), .Q(counter_1_q));  // open: carry
  Comparator #(.width(17), .mode("unsigned")) comparator_1 (
    .a(counter_1_q), .b(17'h186a0), .eq(comparator_1_eq));  // open: gt, lt
  Counter #(.width(2), .max('h3)) counter_2 (
    .clr(Reset), .load(1'b0), .up(1'b1), .count(comparator_1_eq), .clk(Clk), .Q(counter_2_q));  // open: D, carry
  Multiplexer #(.select(2), .width(7)) multiplexer_1 (
    .in0(display0), .in1(display1), .in2(display2), .in3(display3), .out(cathodes), .sel(counter_2_q));  // open: en
  Decoder #(.select(2), .enable("false")) decoder_1 (
    .out0(decoder_1_out0), .out1(decoder_1_out1), .out2(decoder_1_out2), .out3(decoder_1_out3),
    .sel(counter_2_q));
  and and_1 (anode0, decoder_1_out0, enable_display_0);
  and and_2 (anode1, decoder_1_out1, enable_display_1);
  and and_3 (anode2, decoder_1_out2, enable_display_2);
  and and_4 (anode3, decoder_1_out3, enable_display_3);
endmodule

module bytes_display (
  input  [7:0] octet1,
  input  octet1_enable,
  input  [7:0] octet2,
  input  octet2_enable,
  input  reset,
  input  clk,
  output [6:0] cathodes,
  output anode0,
  output anode1,
  output anode2,
  output anode3
);

  wire or_1_out;
  wire [6:0] seven_segments_decode_1_decoded, seven_segments_decode_2_decoded,
       seven_segments_decode_3_decoded, seven_segments_decode_4_decoded;

  seven_segments_decode seven_segments_decode_1 (.Input(octet1[7:4]), .decoded(seven_segments_decode_1_decoded));
  seven_segments_decode seven_segments_decode_3 (.Input(octet1[3:0]), .decoded(seven_segments_decode_3_decoded));
  seven_segments_decode seven_segments_decode_2 (.Input(octet2[7:4]), .decoded(seven_segments_decode_2_decoded));
  seven_segments_decode seven_segments_decode_4 (.Input(octet2[3:0]), .decoded(seven_segments_decode_4_decoded));
  or or_1 (or_1_out, octet1_enable, octet2_enable);
  seven_segment_scan seven_segment_scan_1 (
    .display0(seven_segments_decode_1_decoded), .enable_display_0(octet1_enable),
    .display1(seven_segments_decode_3_decoded), .enable_display_1(octet1_enable),
    .display2(seven_segments_decode_2_decoded), .enable_display_2(octet2_enable),
    .display3(seven_segments_decode_4_decoded), .enable_display_3(octet2_enable), .Reset(reset),
    .Enable(or_1_out), .Clk(clk), .cathodes(cathodes), .anode0(anode0), .anode1(anode1), .anode2(anode2),
    .anode3(anode3));
endmodule
