// Logisim project sin.circ as structural Verilog: 2 circuits, main circuit full_sin_lut
module full_sin_lut (
  input  [10:0] addr,
  output [15:0] data
);

  // sin_lut sin_lut_1: pin names not known; wires that end beside it: addr, data
endmodule

module sin_lut (
  input  [8:0] addr,
  output [15:0] data
);
endmodule
