// Logisim project sound_gen.circ as structural Verilog: 8 circuits, main circuit wave_gen
module wave_gen (
  input  clk,
  input  [15:0] phase_add,
  input  [7:0] waveform,
  output [15:0] sound
);

  wire [15:0] sawtooth_1_sound, sin_1_sound, square_1_sound, triangle_1_sound;
  wire [25:0] adder_1_out, bit_extender_1_out, phase_q;

  assign bit_extender_1_out = {{10{phase_add[15]}}, phase_add};  // Bit_Extender bit_extender_1
  Adder #(.width(26)) adder_1 (.a(bit_extender_1_out), .b(phase_q), .out(adder_1_out), .cin(1'b0));  // open: cout
  Register #(.width(26)) phase (.D(adder_1_out), .en(1'b1), .clk(clk), .Q(phase_q), .clr(1'b0));
  sin sin_1 (.phase(phase_q), .sound(sin_1_sound));
  square square_1 (.phase(phase_q), .sound(square_1_sound));
  sawtooth sawtooth_1 (.phase(phase_q), .sound(sawtooth_1_sound));
  triangle triangle_1 (.phase(phase_q), .sound(triangle_1_sound));
  Multiplexer #(.select(2), .width(16), .enable("false")) multiplexer_1 (
    .in0(sin_1_sound), .in1(square_1_sound), .in2(sawtooth_1_sound), .in3(triangle_1_sound), .out(sound),
    .sel(waveform[1:0]));
endmodule

module square (
  input  [25:0] phase,
  output [15:0] sound
);

  Multiplexer #(.width(16), .enable("false")) multiplexer_1 (
    .in0(16'h7fff), .in1(16'h8001), .out(sound), .sel(phase[25]));
endmodule

module sin (
  input  [25:0] phase,
  output [15:0] sound
);

  full_sin_lut full_sin_lut_1 (.addr(phase[25:15]), .data(sound));
endmodule

module amplitude (
  input  [15:0] sound_in,
  input  [15:0] amplitude,
  output [15:0] sound_amplified
);

  // VHDL_Entity #(.content("library ieee;\n  use ieee.std_logic_1164.all;\n  use ieee.numeric_std.all;\n\nentity Amplifier is\n  port(\n      sound_in: in std_logic_vector(15 downto 0);\n      amplitude: in std_logic_vector(15 downto 0);\n      sound_amplified: out std_logic_vector(15 downto 0)\n    );\nend Amplifier;\n\narchitecture Combinatorial of Amplifier is\n    signal mult_result: signed(32 downto 0);\nbegin\n      mult_result <= signed(sound_in) * signed(amplitude);\n      sound_amplified <= std_logic_vector(shift_left(shift_right(mult_result, 16), 1));\nend Combinatorial;")) amplifier_1: pin names not known; wires that end beside it: sound_in, amplitude, sound_amplified
endmodule

module sawtooth (
  input  [25:0] phase,
  output [15:0] sound
);


  assign sound = phase[25:10];
endmodule

module triangle (
  input  [25:0] phase,
  output [15:0] sound
);

  wire [0:0] subtractor_1_out;
  wire [16:0] multiplexer_1_out, negator_1_out;

  Negator #(.width(17)) negator_1 (.in(phase[25:9]), .out(negator_1_out));
  Multiplexer #(.width(17), .enable("false")) multiplexer_1 (
    .in0(phase[25:9]), .in1(negator_1_out), .out(multiplexer_1_out), .sel(phase[25]));
  Subtractor #(.width(17)) subtractor_1 (
    .a(multiplexer_1_out), .b(17'h3fff), .out({sound, subtractor_1_out[0]}));  // open: bin, bout
endmodule

module sound_gen (
  input  clk,
  input  [15:0] phase_add,
  input  [7:0] waveform,
  input  [15:0] amplitude_in,
  output [15:0] sound
);

  wire [15:0] register_1_q, wave_gen_1_sound;

  wave_gen wave_gen_1 (.clk(clk), .phase_add(phase_add), .waveform(waveform), .sound(wave_gen_1_sound));
  Register #(.width(16)) register_1 (.D(wave_gen_1_sound), .en(1'b1), .clk(clk), .Q(register_1_q));  // open: clr
  amplitude amplitude_1 (.sound_in(register_1_q), .amplitude(amplitude_in), .sound_amplified(sound));
endmodule

module soun_gen_ring_modulator (
  input  clk,
  input  [15:0] phase_add,
  input  [7:0] waveform,
  input  [15:0] amplitude_in,
  input  [15:0] phase_add_ring,
  output [15:0] sound
);

  wire [15:0] multiplexer_1_out, multiplexer_2_out, register_1_q, sound_gen_1_sound, sound_gen_2_sound;

  Multiplexer #(.width(16), .enable("false")) multiplexer_1 (
    .in0(amplitude_in), .in1(16'h7fff), .out(multiplexer_1_out), .sel(waveform[6]));
  sound_gen sound_gen_1 (
    .clk(clk), .phase_add(phase_add_ring), .waveform({8{1'b0}}), .amplitude_in(multiplexer_1_out),
    .sound(sound_gen_1_sound));
  Register #(.width(16)) register_1 (.D(multiplexer_2_out), .en(1'b1), .clk(clk), .Q(register_1_q));  // open: clr
  Multiplexer #(.width(16), .enable("false")) multiplexer_2 (
    .in0(multiplexer_1_out), .in1(sound_gen_1_sound), .out(multiplexer_2_out), .sel(waveform[2]));
  sound_gen sound_gen_2 (
    .clk(clk), .phase_add(phase_add), .waveform(waveform), .amplitude_in(register_1_q),
    .sound(sound_gen_2_sound));
  Multiplexer #(.width(16), .enable("false")) multiplexer_3 (
    .in0(sound_gen_2_sound), .in1({16{1'b0}}), .out(sound), .sel(waveform[7]));
endmodule
